// Logisim project ALU.circ as structural Verilog: 12 circuits, main circuit main
// ALU
module main (
  input  [31:0] ALU_SOURCE_X,
  input  [31:0] ALU_SOURCE_Y,
  input  [3:0] ALU_OPERATION,
  output LT,
  output EQ,
  output GT,
  output [31:0] ALU_RESULT,
  output ADD_OVERFLOW,
  output SUB_OVERFLOW,
  output DIV_BY_ZERO
);

  wire add_1_add_overflow, div_1_div_by_0, multiplexer_2_out, sub_1_sub_overflow_signal;
  wire [1:0] selectforoverf_1_out_2;
  wire [31:0] add_1_output, and_1_output, div_1_output, mul_1_output, or_1_output, set_1_output,
       sll_1_output, srl_1_output, sub_1_output, xor_1_output;

  sll sll_1 (.Input_X(ALU_SOURCE_X), .Input_Y(ALU_SOURCE_Y), .Output(sll_1_output));
  srl srl_1 (.Input_X(ALU_SOURCE_X), .Input_Y(ALU_SOURCE_Y), .Output(srl_1_output));
  \and  and_1 (.Input_X(ALU_SOURCE_X), .Input_Y(ALU_SOURCE_Y), .Output(and_1_output));
  \or  or_1 (.Input_X(ALU_SOURCE_X), .Input_Y(ALU_SOURCE_Y), .Output(or_1_output));
  \xor  xor_1 (.Input_X(ALU_SOURCE_X), .Input_Y(ALU_SOURCE_Y), .Output(xor_1_output));
  set set_1 (.Input_X(ALU_SOURCE_X), .Input_Y(ALU_SOURCE_Y), .Output(set_1_output));
  mul mul_1 (.Input_X(ALU_SOURCE_X), .Input_Y(ALU_SOURCE_Y), .Output(mul_1_output));
  div div_1 (.Input_X(ALU_SOURCE_X), .Input_Y(ALU_SOURCE_Y), .Output(div_1_output), .div_by_0(div_1_div_by_0));
  sub sub_1 (
    .Input_X(ALU_SOURCE_X), .Input_Y(ALU_SOURCE_Y), .sub_overflow_signal(sub_1_sub_overflow_signal),
    .Output(sub_1_output));
  add add_1 (.Input_X(ALU_SOURCE_X), .Input_Y(ALU_SOURCE_Y), .add_overflow(add_1_add_overflow), .Output(add_1_output));
  Comparator #(.width(32)) comparator_1 (.a(ALU_SOURCE_X), .b(ALU_SOURCE_Y), .gt(GT), .eq(EQ), .lt(LT));
  Multiplexer #(.select(4), .width(32)) multiplexer_1 (
    .in0(sll_1_output), .in1(srl_1_output), .in2(and_1_output), .in3(or_1_output), .in4(xor_1_output),
    .in5(set_1_output), .in6(mul_1_output), .in7(div_1_output), .in8(sub_1_output), .in9(add_1_output),
    .in10(add_1_output), .in11(add_1_output), .in12(add_1_output), .in13(add_1_output), .in14(add_1_output),
    .in15(add_1_output), .out(ALU_RESULT), .sel(ALU_OPERATION));  // open: en
  Multiplexer #(.select(2)) multiplexer_2 (
    .in0(div_1_div_by_0), .in1(sub_1_sub_overflow_signal), .in2(add_1_add_overflow), .out(multiplexer_2_out),
    .sel(selectforoverf_1_out_2));  // open: in3, en
  Demultiplexer #(.select(2)) demultiplexer_1 (
    .out0(DIV_BY_ZERO), .out1(SUB_OVERFLOW), .out2(ADD_OVERFLOW), .in(multiplexer_2_out),
    .sel(selectforoverf_1_out_2));  // open: out3, en
  selectForOverF selectforoverf_1 (.in_1(ALU_OPERATION), .out_2(selectforoverf_1_out_2));

  // Notes on the sheet:
  //   ALU MODULE
endmodule

// SLL
module sll (
  input  [31:0] Input_X,
  input  [31:0] Input_Y,
  output [31:0] Output
);

  Shifter #(.width(32)) shifter_1 (.in(Input_X), .\dist (Input_Y[4:0]), .out(Output));
endmodule

// SRL
module srl (
  input  [31:0] Input_X,
  input  [31:0] Input_Y,
  output [31:0] Output
);

  Shifter #(.width(32), .shift("lr")) shifter_1 (.in(Input_X), .\dist (Input_Y[4:0]), .out(Output));
endmodule

// AND
module \and  (
  input  [31:0] Input_X,
  input  [31:0] Input_Y,
  output [31:0] Output
);

  assign Output = Input_X & Input_Y;  // AND_Gate and_1, 32 bits wide
endmodule

// OR
module \or  (
  input  [31:0] Input_X,
  input  [31:0] Input_Y,
  output [31:0] Output
);

  assign Output = Input_X | Input_Y;  // OR_Gate or_1, 32 bits wide
endmodule

// XOR
module \xor  (
  input  [31:0] Input_X,
  input  [31:0] Input_Y,
  output [31:0] Output
);

  assign Output = Input_X ^ Input_Y;  // XOR_Gate xor_1, 32 bits wide
endmodule

// SET
module set (
  input  [31:0] Input_X,
  input  [31:0] Input_Y,
  output [31:0] Output
);

  wire [31:0] and_1_out, shifter_1_out;

  assign and_1_out = Input_X & 32'hffff;  // AND_Gate and_1, 32 bits wide
  Shifter #(.width(32)) shifter_1 (.in(Input_Y), .\dist (5'b10000), .out(shifter_1_out));
  assign Output = and_1_out | shifter_1_out;  // OR_Gate or_1, 32 bits wide
endmodule

// MUL
module mul (
  input  [31:0] Input_X,
  input  [31:0] Input_Y,
  output [31:0] Output
);

  Multiplier #(.width(32)) multiplier_1 (.a(Input_X), .b(Input_Y), .out(Output));  // open: cin, cout
endmodule

// DIV
module div (
  input  [31:0] Input_X,
  input  [31:0] Input_Y,
  output [31:0] Output,
  output div_by_0
);

  wire xor_1_out;
  wire [31:0] divider_1_out, multiplexer_1_out, multiplexer_2_out, negator_1_out, negator_2_out,
       negator_3_out;

  // Probe on Input_Y
  // Probe on Input_X
  Negator #(.width(32)) negator_1 (.in(Input_X), .out(negator_1_out));
  Multiplexer #(.width(32)) multiplexer_1 (
    .in0(Input_X), .in1(negator_1_out), .out(multiplexer_1_out), .sel(Input_X[31]));  // open: en
  Negator #(.width(32)) negator_2 (.in(Input_Y), .out(negator_2_out));
  Multiplexer #(.width(32)) multiplexer_2 (
    .in0(Input_Y), .in1(negator_2_out), .out(multiplexer_2_out), .sel(Input_Y[31]));  // open: en
  Comparator #(.width(32)) comparator_1 (.a(Input_Y), .b({32{1'b0}}), .eq(div_by_0));  // open: gt, lt
  Divider #(.width(32)) divider_1 (
    .a(multiplexer_1_out), .b(multiplexer_2_out), .out(divider_1_out));  // open: upper, rem
  Negator #(.width(32)) negator_3 (.in(divider_1_out), .out(negator_3_out));
  xor xor_1 (xor_1_out, Input_X[31], Input_Y[31]);
  Multiplexer #(.width(32)) multiplexer_3 (
    .in0(divider_1_out), .in1(negator_3_out), .out(Output), .sel(xor_1_out));  // open: en
  // Probe on Output
endmodule

// SUB
module sub (
  input  [31:0] Input_X,
  input  [31:0] Input_Y,
  output sub_overflow_signal,
  output [31:0] Output
);

  wire and_1_out, and_2_out, and_3_out, and_4_out, comparator_1_gt, comparator_1_lt, comparator_2_gt,
       comparator_2_lt, comparator_3_gt, comparator_3_lt;

  Subtractor #(.width(32)) subtractor_1 (.a(Input_Y), .b(Input_X), .out(Output));  // open: bin, bout
  Comparator #(.width(32)) comparator_1 (
    .a(Input_X), .b({32{1'b0}}), .gt(comparator_1_gt), .lt(comparator_1_lt));  // open: eq
  Comparator #(.width(32)) comparator_2 (
    .a(Output), .b({32{1'b0}}), .gt(comparator_2_gt), .lt(comparator_2_lt));  // open: eq
  Comparator #(.width(32)) comparator_3 (
    .a(Input_Y), .b({32{1'b0}}), .gt(comparator_3_gt), .lt(comparator_3_lt));  // open: eq
  and and_1 (and_1_out, comparator_1_gt, comparator_3_lt);
  and and_2 (and_2_out, comparator_1_lt, comparator_3_gt);
  and and_3 (and_3_out, comparator_2_gt, and_1_out);
  and and_4 (and_4_out, and_2_out, comparator_2_lt);
  or or_1 (sub_overflow_signal, and_4_out, and_3_out);
endmodule

// ADD
module add (
  input  [31:0] Input_X,
  input  [31:0] Input_Y,
  output add_overflow,
  output [31:0] Output
);

  wire and_1_out, and_2_out, and_3_out, and_4_out, and_5_out, comparator_1_gt, comparator_1_lt,
       comparator_2_eq, comparator_2_gt, comparator_2_lt, comparator_3_gt, comparator_3_lt;

  Adder #(.width(32)) adder_1 (.a(Input_X), .b(Input_Y), .out(Output));  // open: cin, cout
  Comparator #(.width(32)) comparator_1 (
    .a(Input_X), .b({32{1'b0}}), .gt(comparator_1_gt), .lt(comparator_1_lt));  // open: eq
  Comparator #(.width(32)) comparator_2 (
    .a(Output), .b({32{1'b0}}), .gt(comparator_2_gt), .eq(comparator_2_eq), .lt(comparator_2_lt));
  Comparator #(.width(32)) comparator_3 (
    .a(Input_Y), .b({32{1'b0}}), .gt(comparator_3_gt), .lt(comparator_3_lt));  // open: eq
  and and_1 (and_1_out, comparator_1_gt, comparator_3_gt);
  and and_2 (and_2_out, comparator_1_lt, comparator_3_lt);
  and and_3 (and_3_out, and_1_out, comparator_2_lt);
  and and_4 (and_4_out, comparator_2_eq, and_2_out);
  and and_5 (and_5_out, comparator_2_gt, and_2_out);
  or or_1 (add_overflow, and_3_out, and_4_out, and_5_out);
endmodule

module selectForOverF (
  input  [3:0] in_1,
  output [1:0] out_2
);

  wire and_1_out, and_2_out, and_3_out, and_4_out, not_1_out, not_2_out, not_3_out, not_4_out, not_5_out,
       not_6_out, not_7_out, not_8_out, not_9_out;

  not not_1 (not_1_out, in_1[3]);
  not not_2 (not_2_out, in_1[1]);
  not not_3 (not_3_out, in_1[2]);
  not not_4 (not_4_out, in_1[0]);
  not not_5 (not_5_out, in_1[1]);
  not not_6 (not_6_out, in_1[2]);
  and and_1 (and_1_out, in_1[0], in_1[1], in_1[2], not_1_out);
  assign out_2 = and_2_out ? 2'b10 : 2'bz;  // Controlled_Buffer controlled_buffer_1
  and and_2 (and_2_out, in_1[0], not_2_out, not_3_out, in_1[3]);
  assign out_2 = and_3_out ? 2'b01 : 2'bz;  // Controlled_Buffer controlled_buffer_2
  and and_3 (and_3_out, not_4_out, not_5_out, not_6_out, in_1[3]);
  assign out_2 = and_1_out ? 2'b00 : 2'bz;  // Controlled_Buffer controlled_buffer_3
  not not_7 (not_7_out, and_2_out);
  and and_4 (and_4_out, not_7_out, not_8_out, not_9_out);
  not not_8 (not_8_out, and_3_out);
  not not_9 (not_9_out, and_1_out);
  assign out_2 = and_4_out ? 2'b11 : 2'bz;  // Controlled_Buffer controlled_buffer_4
endmodule
