// Logisim project CMP.circ as structural Verilog: 1 circuit, main circuit main
// CMP
module main (
  input  LT,
  input  EQ,
  input  GT,
  input  [2:0] CQ_QUERY,
  input  CR_WRITE,
  input  CLOCK,
  output [2:0] CR_VAL,
  output CQ_PASSED
);

  wire _003, _005, _006, nor_1_out, not_1_out, register_2_q;
  wire [2:0] controlled_buffer_1_out, register_1_q;

  or or_1 (_003, CR_VAL[0], CR_VAL[1]);
  or or_2 (_005, CR_VAL[0], CR_VAL[2]);
  or or_3 (_006, CR_VAL[1], CR_VAL[2]);
  assign controlled_buffer_1_out = CR_WRITE ? {LT, EQ, GT} : 3'bz;  // Controlled_Buffer controlled_buffer_1
  Register #(.width(3)) register_1 (.D(controlled_buffer_1_out), .Q(register_1_q), .clk(CLOCK));  // open: en, clr
  not not_1 (not_1_out, nor_1_out);
  Register #(.width(1)) register_2 (.D(not_1_out), .Q(register_2_q), .clk(CLOCK));  // open: en, clr
  Multiplexer #(.width(3)) multiplexer_1 (.in0(register_1_q), .in1(3'b111), .out(CR_VAL), .sel(nor_1_out));  // open: en
  nor nor_1 (nor_1_out, CR_WRITE, register_2_q);
  Multiplexer #(.select(3)) multiplexer_2 (
    .in0(1'b0), .in1(CR_VAL[0]), .in2(CR_VAL[1]), .in3(_003), .in4(CR_VAL[2]), .in5(_005), .in6(_006),
    .in7(1'b1), .out(CQ_PASSED), .sel(CQ_QUERY));  // open: en

  // Other names for the same wires on the sheet: CQ[2:0] = CQ_QUERY; _001 = CR_VAL[0]; GT_t = CR_VAL[0];
  //   _002 = CR_VAL[1]; EQ_t = CR_VAL[1]; _004 = CR_VAL[2]; LT_t = CR_VAL[2]

  // Notes on the sheet:
  //   CR MODULE
endmodule
