// Logisim project CPU.circ as structural Verilog: 6 circuits, main circuit main
// CPU
module main (
  input  [31:0] INSTRUCTION,
  input  [23:0] CURRENT_PC,
  input  CQ_PASSED,
  input  [31:0] REG_1_VAL,
  input  [31:0] REG_2_VAL,
  input  [31:0] REG_3_VAL,
  input  [31:0] ALU_RESULT,
  input  [31:0] MEM_OUT,
  output [23:0] JUMP_ADDRESS,
  output [2:0] CQ_QUERY,
  output CR_WRITE,
  output [3:0] REG_1_READ,
  output [3:0] REG_2_READ,
  output [3:0] REG_3_WRITE,
  output [31:0] REG_WRITE_VAL,
  output REG_WRITE,
  output [31:0] ALU_SOURCE_X,
  output [31:0] ALU_SOURCE_Y,
  output [3:0] ALU_OPERATION,
  output [23:0] MEM_ADDR,
  output [31:0] MEM_IN,
  output MEM_WRITE
);

  wire _24, and_1_out, and_2_out, is1Arg, is2Arg, is3Arg, not_1_out, not_2_out, not_3_out, not_4_out,
       reg_writesig_1_writesig;
  wire [1:0] alusoux_1_output, whichtowrite_1_out_2;
  wire [3:0] RD, RI, RS;
  wire [15:0] Imm16;
  wire [19:0] Imm20;
  wire [23:0] bit_extender_3_out, Imm24;
  wire [31:0] bit_extender_1_out, bit_extender_2_out, bit_extender_4_out, bit_extender_5_out,
       multiplexer_1_out, multiplexer_2_out;

  assign REG_1_READ = not_1_out ? RI : 4'bz;  // Controlled_Buffer controlled_buffer_1
  not not_1 (not_1_out, _24);
  assign REG_3_WRITE = not_2_out ? RD : 4'bz;  // Controlled_Buffer controlled_buffer_2
  not not_2 (not_2_out, is1Arg);
  assign bit_extender_1_out = {{12{Imm20[19]}}, Imm20};  // Bit_Extender bit_extender_1
  assign bit_extender_2_out = {{8{CURRENT_PC[23]}}, CURRENT_PC};  // Bit_Extender bit_extender_2
  Bit_Extender #(.in_width(32), .out_width(24)) bit_extender_3 (.in(REG_1_VAL), .out(bit_extender_3_out));
  not not_3 (not_3_out, ALU_OPERATION[1]);
  Multiplexer #(.width(32), .enable("false")) multiplexer_1 (
    .in0(REG_1_VAL), .in1(bit_extender_1_out), .out(multiplexer_1_out), .sel(_24));
  assign bit_extender_4_out = {{16{Imm16[15]}}, Imm16};  // Bit_Extender bit_extender_4
  Multiplexer #(.width(32), .enable("false")) multiplexer_2 (
    .in0(bit_extender_4_out), .in1(bit_extender_5_out), .out(multiplexer_2_out), .sel(is2Arg));
  assign bit_extender_5_out = {{12{Imm20[19]}}, Imm20};  // Bit_Extender bit_extender_5
  Bit_Extender #(.in_width(32), .out_width(24)) bit_extender_6 (.in(ALU_RESULT), .out(MEM_ADDR));
  not not_4 (not_4_out, ALU_OPERATION[2]);
  Multiplexer #(.width(24), .enable("false")) multiplexer_3 (
    .in0(bit_extender_3_out), .in1(Imm24), .out(JUMP_ADDRESS), .sel(_24));
  Multiplexer #(.enable("false")) multiplexer_4 (.in0(1'b0), .in1(and_1_out), .out(CR_WRITE), .sel(CQ_PASSED));
  and and_1 (and_1_out, ALU_OPERATION[0], not_3_out, ALU_OPERATION[2], ALU_OPERATION[3]);
  assign REG_2_READ = is3Arg ? RS : 4'bz;  // Controlled_Buffer controlled_buffer_3
  whichtoWrite whichtowrite_1 (.opcode(ALU_OPERATION), .out_2(whichtowrite_1_out_2));
  Reg_writeSig reg_writesig_1 (.opcode(ALU_OPERATION), .writeSig(reg_writesig_1_writesig));
  ALUsouX alusoux_1 (.opcode(ALU_OPERATION), .\output (alusoux_1_output));
  Multiplexer #(.width(32), .enable("false")) multiplexer_5 (
    .in0(REG_1_VAL), .in1(multiplexer_2_out), .out(ALU_SOURCE_Y), .sel(_24));
  and and_2 (and_2_out, ALU_OPERATION[0], ALU_OPERATION[1], not_4_out, ALU_OPERATION[3]);
  Multiplexer #(.select(2), .width(32), .enable("false")) multiplexer_6 (
    .in0(ALU_RESULT), .in1(MEM_OUT), .in2(multiplexer_1_out), .out(REG_WRITE_VAL), .sel(whichtowrite_1_out_2));  // open: in3
  Multiplexer #(.enable("false")) multiplexer_7 (
    .in0(1'b0), .in1(reg_writesig_1_writesig), .out(REG_WRITE), .sel(CQ_PASSED));
  Multiplexer #(.select(2), .width(32), .enable("false")) multiplexer_8 (
    .in0(REG_2_VAL), .in1(REG_3_VAL), .in2(bit_extender_2_out), .out(ALU_SOURCE_X), .sel(alusoux_1_output));  // open: in3
  Multiplexer #(.enable("false")) multiplexer_9 (.in0(1'b0), .in1(and_2_out), .out(MEM_WRITE), .sel(CQ_PASSED));
  InstructionSeparater instructionseparater_1 (
    .InstInput(INSTRUCTION), .opcode(ALU_OPERATION), .RI(RI), .CQ(CQ_QUERY), .RD(RD), ._24(_24), .RS(RS),
    .Im24(Imm24), .Im20(Imm20), .Im16(Imm16), .is1ARG(is1Arg), .is2ARG(is2Arg), .is3ARG(is3Arg));

  assign MEM_IN = REG_3_VAL;

  // Other names for the same wires on the sheet: ALU_res[31:0] = ALU_RESULT; CQ[2:0] = CQ_QUERY; CQpass = CQ_PASSED;
  //   mem_outVal[31:0] = MEM_OUT; opcode[3:0] = ALU_OPERATION; PCval[23:0] = CURRENT_PC; RDvalue[31:0] = REG_3_VAL;
  //   RIvalue[31:0] = REG_1_VAL; RSvalue[31:0] = REG_2_VAL

  // Notes on the sheet:
  //   INSTRUCTION MODULE
  //   CR MODULE
  //   REGISTER FILE MODULE
  //   ALU MODULE
  //   MEMORY MODULE
endmodule

module InstructionSeparater (
  input  [31:0] InstInput,
  output [3:0] opcode,
  output [3:0] RI,
  output [2:0] CQ,
  output [3:0] RD,
  output _24,
  output [3:0] RS,
  output [23:0] Im24,
  output [19:0] Im20,
  output [15:0] Im16,
  output is1ARG,
  output is2ARG,
  output is3ARG
);

  wire and_1_out, and_3_out, and_4_out, and_5_out, not_2_out, not_3_out, not_4_out, not_5_out, not_6_out,
       not_7_out;

  and and_1 (and_1_out, InstInput[30], InstInput[31]);
  and and_2 (is1ARG, InstInput[28], InstInput[29], InstInput[30], InstInput[31]);
  not not_1 (is3ARG, and_1_out);
  not not_2 (not_2_out, is1ARG);
  not not_3 (not_3_out, is3ARG);
  assign RI = not_4_out ? InstInput[3:0] : 4'bz;  // Controlled_Buffer controlled_buffer_1
  not not_4 (not_4_out, InstInput[24]);
  assign RD = not_5_out ? InstInput[23:20] : 4'bz;  // Controlled_Buffer controlled_buffer_2
  not not_5 (not_5_out, is1ARG);
  assign RS = is3ARG ? InstInput[19:16] : 4'bz;  // Controlled_Buffer controlled_buffer_3
  assign Im24 = and_3_out ? InstInput[23:0] : 24'bz;  // Controlled_Buffer controlled_buffer_4
  and and_3 (and_3_out, InstInput[24], is1ARG);
  and and_4 (and_4_out, not_2_out, InstInput[24], not_3_out);
  assign Im16 = and_5_out ? InstInput[15:0] : 16'bz;  // Controlled_Buffer controlled_buffer_5
  and and_5 (and_5_out, is3ARG, InstInput[24]);
  not not_6 (not_6_out, is1ARG);
  not not_7 (not_7_out, is3ARG);
  assign Im20 = and_4_out ? InstInput[19:0] : 20'bz;  // Controlled_Buffer controlled_buffer_6
  and and_6 (is2ARG, not_6_out, not_7_out);

  assign _24 = InstInput[24];
  assign CQ = InstInput[27:25];
  assign opcode = InstInput[31:28];
endmodule

module Reg_writeSig (
  input  [3:0] opcode,
  output writeSig
);

  wire and_1_out, and_2_out, or_1_out, xor_1_out;

  xor xor_1 (xor_1_out, opcode[1], opcode[2]);
  and and_1 (and_1_out, opcode[2], opcode[1]);
  or or_1 (or_1_out, xor_1_out, and_1_out);
  and and_2 (and_2_out, opcode[0], or_1_out, opcode[3]);
  not not_1 (writeSig, and_2_out);
endmodule

module whichtoWrite (
  input  [3:0] opcode,
  output [1:0] out_2
);

  wire not_1_out, not_2_out, not_3_out;

  not not_1 (not_1_out, opcode[0]);
  not not_2 (not_2_out, opcode[2]);
  not not_3 (not_3_out, opcode[1]);
  and and_1 (out_2[1], not_1_out, not_3_out, opcode[2], opcode[3]);
  and and_2 (out_2[0], not_1_out, opcode[1], not_2_out, opcode[3]);
endmodule

module ALUsouX (
  input  [3:0] opcode,
  output [1:0] \output 
);

  wire not_1_out, not_2_out;

  not not_1 (not_1_out, opcode[1]);
  not not_2 (not_2_out, opcode[0]);
  and and_1 (\output [0], opcode[0], not_1_out, opcode[2], opcode[3]);
  and and_2 (\output [1], not_2_out, opcode[1], opcode[2], opcode[3]);
endmodule

module IsSTU (
  input  [3:0] opcode,
  output \output 
);

  wire not_1_out, not_2_out;

  not not_1 (not_1_out, opcode[1]);
  not not_2 (not_2_out, opcode[3]);
  and and_1 (\output , opcode[0], not_1_out, opcode[2], not_2_out);
endmodule
