// Logisim project NPC.circ as structural Verilog: 1 circuit, main circuit main
// NPC
module main (
  input  CQ_PASSED,
  input  [31:0] INSTRUCTION,
  input  [23:0] CURRENT_PC,
  input  [23:0] JUMP_ADDRESS,
  output [23:0] NEXT_PC
);

  wire _1_if_jump_out, and_1_out, and_2_out, JorNot;
  wire [23:0] adder_1_out;

  and and_1 (and_1_out, INSTRUCTION[25], INSTRUCTION[26], INSTRUCTION[27]);
  and and_2 (and_2_out, INSTRUCTION[28], INSTRUCTION[29], INSTRUCTION[30], INSTRUCTION[31]);
  Adder #(.width(24)) adder_1 (.a(CURRENT_PC), .b(24'h1), .out(adder_1_out));  // open: cin, cout
  or _1_if_jump (_1_if_jump_out, CQ_PASSED, and_1_out);
  Multiplexer #(.width(24)) multiplexer_1 (
    .in0(adder_1_out), .in1(JUMP_ADDRESS), .out(NEXT_PC), .sel(JorNot));  // open: en
  and and_3 (JorNot, _1_if_jump_out, and_2_out);

  // Notes on the sheet:
  //   NPC MODULE
endmodule
