// Logisim project PIP.circ as structural Verilog: 1 circuit, main circuit main
// PIP
module main (
  input  CQ_PASSED,
  input  [31:0] INSTRUCTION_IN,
  input  [23:0] PC_IN,
  input  CLOCK,
  output [31:0] INSTRUCTION_OUT,
  output [23:0] PC_OUT
);

  wire and_1_out, indecator;
  wire [31:0] multiplexer_1_out;

  and and_1 (and_1_out, INSTRUCTION_OUT[28], INSTRUCTION_OUT[29], INSTRUCTION_OUT[30], INSTRUCTION_OUT[31]);
  Multiplexer #(.width(32)) multiplexer_1 (
    .in0(INSTRUCTION_IN), .in1({32{1'b0}}), .out(multiplexer_1_out), .sel(indecator));  // open: en
  Register #(.width(24)) register_1 (.D(PC_IN), .Q(PC_OUT), .clk(CLOCK));  // open: en, clr
  and and_2 (indecator, CQ_PASSED, and_1_out);
  Register #(.width(32)) register_2 (.D(multiplexer_1_out), .Q(INSTRUCTION_OUT), .clk(CLOCK));  // open: en, clr

  // Other names for the same wires on the sheet: instrOut[31:0] = INSTRUCTION_OUT

  // Notes on the sheet:
  //   PIPELINE MODULE
endmodule
