// Logisim project REG.circ as structural Verilog: 1 circuit, main circuit main
// REG
module main (
  input  CLOCK,
  input  [3:0] REG_1_READ,
  input  [3:0] REG_2_READ,
  input  [3:0] REG_3_WRITE,
  input  [31:0] REG_WRITE_VAL,
  input  REG_WRITE,
  output [31:0] R00,
  output [31:0] R01,
  output [31:0] R02,
  output [31:0] R03,
  output [31:0] R04,
  output [31:0] R05,
  output [31:0] R06,
  output [31:0] R07,
  output [31:0] REG_1_VAL,
  output [31:0] REG_2_VAL,
  output [31:0] REG_3_VAL,
  output [31:0] R08,
  output [31:0] R09,
  output [31:0] R10,
  output [31:0] R11,
  output [31:0] R12,
  output [31:0] R13,
  output [31:0] R14,
  output [31:0] R15
);

  wire [31:0] In00, In01, In02, In03, In04, In05, In06, In07, In08, In09, In10, In11, In12, In13, In14, In15,
       wrVal;

  assign wrVal = REG_WRITE ? REG_WRITE_VAL : 32'bz;  // Controlled_Buffer controlled_buffer_1
  Demultiplexer #(.select(4), .width(32), .tristate("true")) demultiplexer_1 (
    .out0(In00), .out1(In01), .out2(In02), .out3(In03), .out4(In04), .out5(In05), .out6(In06), .out7(In07),
    .out8(In08), .out9(In09), .out10(In10), .out11(In11), .out12(In12), .out13(In13), .out14(In14),
    .out15(In15), .in(wrVal), .sel(REG_3_WRITE));  // open: en
  Register #(.width(32)) u_R00 (.D(In00), .Q(R00), .clk(CLOCK));  // open: en, clr
  Register #(.width(32)) u_R04 (.D(In04), .Q(R04), .clk(CLOCK));  // open: en, clr
  Register #(.width(32)) u_R08 (.D(In08), .Q(R08), .clk(CLOCK));  // open: en, clr
  Register #(.width(32)) u_R12 (.D(In12), .Q(R12), .clk(CLOCK));  // open: en, clr
  Register #(.width(32)) u_R01 (.D(In01), .Q(R01), .clk(CLOCK));  // open: en, clr
  Register #(.width(32)) u_R05 (.D(In05), .Q(R05), .clk(CLOCK));  // open: en, clr
  Register #(.width(32)) u_R09 (.D(In09), .Q(R09), .clk(CLOCK));  // open: en, clr
  Register #(.width(32)) u_R13 (.D(In13), .Q(R13), .clk(CLOCK));  // open: en, clr
  Register #(.width(32)) u_R02 (.D(In02), .Q(R02), .clk(CLOCK));  // open: en, clr
  Register #(.width(32)) u_R06 (.D(In06), .Q(R06), .clk(CLOCK));  // open: en, clr
  Register #(.width(32)) u_R10 (.D(In10), .Q(R10), .clk(CLOCK));  // open: en, clr
  Register #(.width(32)) u_R14 (.D(In14), .Q(R14), .clk(CLOCK));  // open: en, clr
  Register #(.width(32)) u_R03 (.D(In03), .Q(R03), .clk(CLOCK));  // open: en, clr
  Register #(.width(32)) u_R07 (.D(In07), .Q(R07), .clk(CLOCK));  // open: en, clr
  Register #(.width(32)) u_R11 (.D(In11), .Q(R11), .clk(CLOCK));  // open: en, clr
  Register #(.width(32)) u_R15 (.D(In15), .Q(R15), .clk(CLOCK));  // open: en, clr
  Multiplexer #(.select(4), .width(32)) multiplexer_1 (
    .in0(R00), .in1(R01), .in2(R02), .in3(R03), .in4(R04), .in5(R05), .in6(R06), .in7(R07), .in8(R08),
    .in9(R09), .in10(R10), .in11(R11), .in12(R12), .in13(R13), .in14(R14), .in15(R15), .out(REG_3_VAL),
    .sel(REG_3_WRITE));  // open: en
  Multiplexer #(.select(4), .width(32)) multiplexer_2 (
    .in0(R00), .in1(R01), .in2(R02), .in3(R03), .in4(R04), .in5(R05), .in6(R06), .in7(R07), .in8(R08),
    .in9(R09), .in10(R10), .in11(R11), .in12(R12), .in13(R13), .in14(R14), .in15(R15), .out(REG_1_VAL),
    .sel(REG_1_READ));  // open: en
  Multiplexer #(.select(4), .width(32)) multiplexer_3 (
    .in0(R00), .in1(R01), .in2(R02), .in3(R03), .in4(R04), .in5(R05), .in6(R06), .in7(R07), .in8(R08),
    .in9(R09), .in10(R10), .in11(R11), .in12(R12), .in13(R13), .in14(R14), .in15(R15), .out(REG_2_VAL),
    .sel(REG_2_READ));  // open: en

  // Other names for the same wires on the sheet: Read1[3:0] = REG_1_READ; Read2[3:0] = REG_2_READ;
  //   write[3:0] = REG_3_WRITE

  // Notes on the sheet:
  //   REGISTER FILE MODULE
endmodule
