// Logisim project RUN.circ as structural Verilog: 1 circuit, main circuit Run
module Run (
);

  wire clock_1_out, main_3_add_overflow, main_3_div_by_zero, main_3_eq, main_3_gt, main_3_lt,
       main_3_sub_overflow, main_4_cq_passed, main_5_cr_write, main_5_mem_write, main_5_reg_write;
  wire [2:0] CR, main_5_cq_query;
  wire [3:0] main_5_alu_operation, main_5_reg_1_read, main_5_reg_2_read, main_5_reg_3_write;
  wire [23:0] main_1_pc_out, main_5_jump_address, main_5_mem_addr, main_6_next_pc, PC;
  wire [31:0] A0, A1, A2, A3, main_1_instruction_out, main_2_reg_1_val, main_2_reg_2_val, main_2_reg_3_val,
       main_3_alu_result, main_5_alu_source_x, main_5_alu_source_y, main_5_mem_in, main_5_reg_write_val, RA,
       ram_1_data, ram_2_data, RV, SP, T0, T1, T2, T3, T4, T5, T6, T7, T8;

  // Probe on main_1_instruction_out
  // Probe on PC
  // Probe on CR
  // Probe on RV
  // Probe on A0
  // Probe on T0
  // Probe on T5
  // Probe on SP
  RAM #(.addrWidth(24), .dataWidth(32)) ram_1 (.addr(PC), .data(ram_1_data));  // open: sel, clk, ld, clr
  PIP_main main_1 (
    .INSTRUCTION_IN(ram_1_data), .INSTRUCTION_OUT(main_1_instruction_out), .CQ_PASSED(main_4_cq_passed),
    .CLOCK(clock_1_out), .PC_IN(PC), .PC_OUT(main_1_pc_out));
  // Probe on main_1_pc_out
  // Probe on RA
  // Probe on A1
  // Probe on T1
  // Probe on T6
  REG_main main_2 (
    .REG_1_READ(main_5_reg_1_read), .REG_2_READ(main_5_reg_2_read), .REG_3_WRITE(main_5_reg_3_write),
    .REG_WRITE_VAL(main_5_reg_write_val), .REG_WRITE(main_5_reg_write), .REG_1_VAL(main_2_reg_1_val),
    .REG_2_VAL(main_2_reg_2_val), .REG_3_VAL(main_2_reg_3_val), .R00(RV), .R01(RA), .R02(A0), .R03(A1),
    .R04(A2), .R05(A3), .R06(T0), .R07(T1), .R08(T2), .R09(T3), .R10(T4), .R11(T5), .R12(T6), .R13(T7),
    .R14(T8), .R15(SP), .CLOCK(clock_1_out));
  LED led (.in(main_3_add_overflow));
  LED led_2 (.in(main_3_sub_overflow));
  LED led_3 (.in(main_3_div_by_zero));
  ALU_main main_3 (
    .LT(main_3_lt), .EQ(main_3_eq), .GT(main_3_gt), .ALU_SOURCE_X(main_5_alu_source_x),
    .ALU_SOURCE_Y(main_5_alu_source_y), .ALU_RESULT(main_3_alu_result), .ALU_OPERATION(main_5_alu_operation),
    .ADD_OVERFLOW(main_3_add_overflow), .SUB_OVERFLOW(main_3_sub_overflow), .DIV_BY_ZERO(main_3_div_by_zero));
  // Probe on A2
  // Probe on T2
  // Probe on T7
  CMP_main main_4 (
    .CQ_QUERY(main_5_cq_query), .CQ_PASSED(main_4_cq_passed), .LT(main_3_lt), .EQ(main_3_eq), .GT(main_3_gt),
    .CR_VAL(CR), .CR_WRITE(main_5_cr_write), .CLOCK(clock_1_out));
  // Probe on A3
  // Probe on T3
  // Probe on T8
  CPU_main main_5 (
    .INSTRUCTION(main_1_instruction_out), .CQ_PASSED(main_4_cq_passed), .REG_1_VAL(main_2_reg_1_val),
    .ALU_RESULT(main_3_alu_result), .REG_2_VAL(main_2_reg_2_val), .MEM_OUT(ram_2_data),
    .REG_3_VAL(main_2_reg_3_val), .JUMP_ADDRESS(main_5_jump_address), .ALU_SOURCE_X(main_5_alu_source_x),
    .REG_1_READ(main_5_reg_1_read), .REG_2_READ(main_5_reg_2_read), .MEM_ADDR(main_5_mem_addr),
    .REG_3_WRITE(main_5_reg_3_write), .ALU_SOURCE_Y(main_5_alu_source_y), .MEM_IN(main_5_mem_in),
    .REG_WRITE_VAL(main_5_reg_write_val), .ALU_OPERATION(main_5_alu_operation), .CR_WRITE(main_5_cr_write),
    .REG_WRITE(main_5_reg_write), .MEM_WRITE(main_5_mem_write), .CURRENT_PC(main_1_pc_out),
    .CQ_QUERY(main_5_cq_query));
  NPC_main main_6 (
    .JUMP_ADDRESS(main_5_jump_address), .CURRENT_PC(PC), .NEXT_PC(main_6_next_pc),
    .CQ_PASSED(main_4_cq_passed), .INSTRUCTION(main_1_instruction_out));
  Clock clock_1 (.out(clock_1_out));
  RAM #(.addrWidth(24), .dataWidth(32), .bus("separate")) ram_2 (
    .addr(main_5_mem_addr), .din(main_5_mem_in), .data(ram_2_data), .str(main_5_mem_write), .clk(clock_1_out));  // open: sel, ld, clr
  Register #(.width(24)) register_1 (.D(main_6_next_pc), .Q(PC), .clk(clock_1_out));  // open: en, clr
  // Probe on T4

  // Notes on the sheet:
  //   INST MEMORY
  //   DATA MEMORY
endmodule
